# Fritzing sketch layout (saved by Fritzing 0.9.3b)

parts:
  Composant1 = Arduino Motor Shield (Rev3)
  M1 = Stepper Motor - Bipolar
  ZS-042_RTC1 = ZS-042 RTC Module
  S1 = Square Pushbutton
  S2 = Square Pushbutton

nets:
  N1: Composant1.A4, ZS-042_RTC1.SDA
  N2: Composant1.A5, ZS-042_RTC1.SCL
  N3: Composant1.D6_PWM, S1.leg1
  N4: Composant1.D7, S2.leg1
  N5: Composant1.B-, M1.D
  N6: Composant1.B+, M1.B
  N7: Composant1.A-, M1.C
  N8: Composant1.A+, M1.A
  GND: Composant1.GND, ZS-042_RTC1.GND, S1.leg0, S2.leg0
  5V: Composant1.5V, ZS-042_RTC1.VCC
